// Logisim project memdados.circ as structural Verilog: 1 circuit, main circuit datamem
// Mem. dados
module datamem (
  input  MemWrite,
  input  clk,
  input  [31:0] Escreve_dado,
  input  [31:0] Endereco,
  output [31:0] Dados_lidos
);

  RAM #(.addrWidth(24), .asyncread("true"), .dataWidth(32)) ram_1 (
    .addr(Endereco[23:0]), .we(MemWrite), .oe(1'b1), .clk(clk), .din(Escreve_dado), .dout(Dados_lidos));
endmodule
