// Logisim project main.circ as structural Verilog: 1 circuit, main circuit main
module main (
);

  wire ALUSrcB, and_1_out, and_2_out, and_3_out, Auipc, Branch, BranchSrc, CLK, Jalr, Jump, Lui, MemRead,
       MemToReg, MemWrite, PCSrc, RegWrite, Stop, sUnsigned, ucdesvio_1_branchsrc, ucprincipal_1_alusrcb,
       ucprincipal_1_auipc_uc, ucprincipal_1_branch, ucprincipal_1_jump, ucprincipal_1_lui_uc,
       ucprincipal_1_memread, ucprincipal_1_memtoreg, ucprincipal_1_memwrite, ucprincipal_1_pcsrc,
       ucprincipal_1_regwrite, ucprincipal_1_s_jalr, Zero;
  wire [1:0] ALUOp, offset, ucenderecamento_1_size, ucprincipal_1_aluop;
  wire [2:0] decodificador_1_funct3, estagioid_ex_1_f3_ex;
  wire [3:0] ucenderecamento_1_byteenable, ucula_1_p5;
  wire [4:0] decodificador_1_rd, decodificador_1_rs1, decodificador_1_rs2;
  wire [6:0] decodificador_1_funct7, decodificador_1_opcode, estagioid_ex_1_f7_ex, estagioid_ex_1_opcode_ex;
  wire [31:0] adder_1_out, adder_2_out, ALU, bancoregistradores_1_ld1, bancoregistradores_1_ld2,
       contadorciclos_1_contador, decodificador_1_imm, estagioid_ex_1_imm_ex, estagioid_ex_1_pcplus4_ex,
       estagioid_ex_1_rs1_ex, estagioid_ex_1_rs2_ex, estagioif_id_1_p4, estagioif_id_1_p5, Imm, LD1, LD2,
       memdados_1_dados_lidos, meminstr_1_instruction, multiplexer_1_out, multiplexer_2_out,
       multiplexer_3_out, multiplexer_4_out, multiplexer_5_out, PC, PC_q, WD;

  Multiplexer #(.width(32)) multiplexer_1 (
    .in0(adder_2_out), .in1(adder_1_out), .out(multiplexer_1_out), .sel(ucprincipal_1_pcsrc));
  Adder #(.width(32)) adder_1 (.a(PC_q), .b(decodificador_1_imm), .out(adder_1_out));  // open: cin, cout
  // Probe on Imm
  and and_1 (and_1_out, CLK, ~Stop);  // AND_Gate
  // Probe on contadorciclos_1_contador
  contadorCiclos contadorciclos_1 (.Clock(and_1_out), .Contador(contadorciclos_1_contador));
  Clock clock_1 (.out(CLK));
  Register #(.width(32)) u_PC (.D(multiplexer_2_out), .en(and_2_out), .clk(and_2_out), .Q(PC_q));  // open: clr
  Multiplexer #(.width(32)) multiplexer_2 (
    .in0(multiplexer_1_out), .in1(ALU), .out(multiplexer_2_out), .sel(ucprincipal_1_s_jalr));
  and and_2 (and_2_out, CLK, ~Stop);  // AND_Gate
  // Probe on PC
  // Probe on LD1
  // Probe on LD2
  // Probe on ALU
  Adder #(.width(32)) adder_2 (.a(32'h4), .b(PC_q), .out(adder_2_out));  // open: cin, cout
  memInstr meminstr_1 (.PC_address(PC_q), .Instruction(meminstr_1_instruction));
  // estagioIF_ID estagioif_id_1: pin names not known; wires that end beside it: adder_2_out, meminstr_1_instruction, CLK, estagioif_id_1_p4, estagioif_id_1_p5
  decodificador decodificador_1 (
    .instrucao(estagioif_id_1_p5), .imm(decodificador_1_imm), .opcode(decodificador_1_opcode),
    .rd(decodificador_1_rd), .funct3(decodificador_1_funct3), .rs1(decodificador_1_rs1),
    .rs2(decodificador_1_rs2), .funct7(decodificador_1_funct7));
  ucDesvio ucdesvio_1 (.Zero(Zero), .BranchSrc(ucdesvio_1_branchsrc));  // open: funct3
  ucPrincipal ucprincipal_1 (
    .BranchSrc(ucdesvio_1_branchsrc), .opcode(decodificador_1_opcode), .MemRead(ucprincipal_1_memread),
    .MemWrite(ucprincipal_1_memwrite), .Jump(ucprincipal_1_jump), .Branch(ucprincipal_1_branch),
    .S_Jalr(ucprincipal_1_s_jalr), .RegWrite(ucprincipal_1_regwrite), .ALUOp(ucprincipal_1_aluop),
    .Auipc_uc(ucprincipal_1_auipc_uc), .ALUSrcB(ucprincipal_1_alusrcb), .Lui_uc(ucprincipal_1_lui_uc),
    .Stop(Stop), .MemToReg(ucprincipal_1_memtoreg), .PCSrc(ucprincipal_1_pcsrc));
  Multiplexer #(.width(32)) multiplexer_3 (
    .in0(WD), .in1(estagioif_id_1_p4), .out(multiplexer_3_out), .sel(ucprincipal_1_jump));
  bancoRegistradores bancoregistradores_1 (
    .RegWrite(ucprincipal_1_regwrite), .LR1(decodificador_1_rs1), .LR2(decodificador_1_rs2),
    .WD(multiplexer_3_out), .WR(decodificador_1_rd), .clk(CLK), .LD2(bancoregistradores_1_ld2),
    .LD1(bancoregistradores_1_ld1));
  estagioID_EX estagioid_ex_1 (
    .CLK(CLK), .RegWrite_ID(ucprincipal_1_regwrite), .ALUSrcB_ID(ucprincipal_1_alusrcb),
    .Auipc_ID(ucprincipal_1_auipc_uc), .PCSrc_ID(ucprincipal_1_pcsrc), .Jump_ID(ucprincipal_1_jump),
    .Jalr_ID(ucprincipal_1_s_jalr), .ALUOp_ID(ucprincipal_1_aluop), .PCplus4_ID(estagioif_id_1_p4),
    .Lui_ID(ucprincipal_1_lui_uc), .MemToReg_ID(ucprincipal_1_memtoreg), .MemRead_ID(ucprincipal_1_memread),
    .MemWrite_ID(ucprincipal_1_memwrite), .Branch_ID(ucprincipal_1_branch),
    .BranchSrc_ID(ucdesvio_1_branchsrc), .opcode_ID(decodificador_1_opcode),
    .rs1_ID(bancoregistradores_1_ld1), .rs2_ID(bancoregistradores_1_ld2), .f3_ID(decodificador_1_funct3),
    .f7_ID(decodificador_1_funct7), .imm_ID(decodificador_1_imm), .opcode_EX(estagioid_ex_1_opcode_ex),
    .rs1_EX(estagioid_ex_1_rs1_ex), .rs2_EX(estagioid_ex_1_rs2_ex), .f3_EX(estagioid_ex_1_f3_ex),
    .f7_EX(estagioid_ex_1_f7_ex), .imm_EX(estagioid_ex_1_imm_ex), .Auipc_EX(Auipc), .RegWrite_EX(RegWrite),
    .ALUSrcB_EX(ALUSrcB), .PCSrc_EX(PCSrc), .Jump_EX(Jump), .Jalr_EX(Jalr), .ALUOp_EX(ALUOp),
    .MemWrite_EX(MemWrite), .MemToReg_EX(MemToReg), .Lui_EX(Lui), .MemRead_EX(MemRead), .Branch_EX(Branch),
    .BranchSrc_EX(BranchSrc), .PCplus4_EX(estagioid_ex_1_pcplus4_ex));
  // ucULA ucula_1: pin names not known; wires that end beside it: estagioid_ex_1_opcode_ex, estagioid_ex_1_f3_ex, estagioid_ex_1_f7_ex, ALUOp, ucula_1_p5
  Multiplexer #(.width(32)) multiplexer_4 (.in0(estagioid_ex_1_rs1_ex), .in1(PC), .out(multiplexer_4_out), .sel(Auipc));
  Multiplexer #(.width(32)) multiplexer_5 (
    .in0(multiplexer_4_out), .in1({32{1'b0}}), .out(multiplexer_5_out), .sel(Lui));
  Multiplexer #(.width(32)) multiplexer_6 (
    .in0(estagioid_ex_1_rs2_ex), .in1(estagioid_ex_1_imm_ex), .out(LD2), .sel(ALUSrcB));
  ULA ula_1 (.B(LD2), .ALUControl(ucula_1_p5), .A(multiplexer_5_out), .sZero(Zero), .Result(ALU));
  ucEnderecamento ucenderecamento_1 (
    .Adress(ALU), .Funct3(estagioid_ex_1_f3_ex), .writeEnable(MemWrite),
    .byteEnable(ucenderecamento_1_byteenable), .Size(ucenderecamento_1_size), .Offset(offset),
    .signal_unsigned(sUnsigned));
  and and_3 (and_3_out, CLK, ~Stop);  // AND_Gate
  memDados memdados_1 (
    .Endereco(ALU), .clk(and_3_out), .MemRead(MemRead), .byteEnable(ucenderecamento_1_byteenable),
    .dado(estagioid_ex_1_rs2_ex), .size(ucenderecamento_1_size), .offset(offset), .sUnsigned(sUnsigned),
    .Dados_lidos(memdados_1_dados_lidos));
  Multiplexer #(.width(32)) multiplexer_7 (.in0(ALU), .in1(memdados_1_dados_lidos), .out(WD), .sel(MemToReg));

  // Notes on the sheet:
  //   rs2
  //   PC + 4
  //   Imm
endmodule
