// Logisim project ImmGen.circ as structural Verilog: 1 circuit, main circuit immGen
module immGen (
  input  [31:0] \instrução ,
  input  [1:0] ImmSrc,
  output [31:0] imm
);

  wire [31:0] undriven, undriven_2, undriven_3, undriven_4;

  // extensorSinal_12 extensorsinal_12_1: pin names not known; wires that end beside it: \instrução [31:20]
  // extensorSinal_12 extensorsinal_12_2: pin names not known; wires that end beside it: {\instrução [31:25], \instrução [11:7]}
  // extensorSinal_13 extensorsinal_13_1: pin names not known; wires that end beside it: {\instrução [31], \instrução [7], \instrução [30:25], \instrução [11:8], 1'b0}
  // extensorSinal_21 extensorsinal_21_1: pin names not known; wires that end beside it: {\instrução [31], \instrução [19:12], \instrução [20], \instrução [30:21], 1'b0}
  // extensorSinal_20 extensorsinal_20_1: pin names not known; wires that end beside it: \instrução [31:12]
  // Probe on imm
  Multiplexer #(.select(2), .width(32), .enable("false")) multiplexer_1 (
    .in0(undriven), .in1(undriven_2), .in2(undriven_3), .in3(undriven_4), .out(imm), .sel(ImmSrc));

  // Other names for the same wires on the sheet: B_type_imm[12:1] = {\instrução [31], \instrução [7], \instrução [30:25], \instrução [11:8]};
  //   imm_5[4:0] = \instrução [11:7]; S_type_imm[11:0] = {\instrução [31:25], \instrução [11:7]};
  //   I_type_imm[11:0] = \instrução [31:20]; imm_12[11:0] = \instrução [31:20]; imm_20[19:0] = \instrução [31:12];
  //   J_type_imm[20:1] = {\instrução [31], \instrução [19:12], \instrução [20], \instrução [30:21]};
  //   U_type_imm[19:0] = \instrução [31:12]; imm_7[6:0] = \instrução [31:25]

  // Notes on the sheet:
  //   Tipo I
  //   Tipo S
  //   Tipo B
  //   Tipo U
  //   Tipo J
endmodule
