// Logisim project simuladorFinal.circ as structural Verilog: 1 circuit, main circuit main
module main (
);

  wire ALUSrc, Bne, Branch, CLK, Jalr, Jump, MemRead, MemToReg, MemWrite, Neg, PCSrc, RegWrite,
       ula_1_overflow, Zero;
  wire [1:0] ALUOp, ImmSrc;
  wire [2:0] decodificador_1_funct3;
  wire [3:0] ucula_1_alucontrol;
  wire [4:0] decodificador_1_rd, decodificador_1_rs1, decodificador_1_rs2;
  wire [6:0] decodificador_1_funct7, decodificador_1_opcode;
  wire [31:0] adder_1_out, bancoregistradores_1_ld2, contador_1_contador, datamem_1_dados_lidos, Imm, LD1,
       LD2, meminstr_1_instruction, multiplexer_1_out, multiplexer_2_out, multiplexer_3_out, PC, PC___4, ULA,
       WD;

  Adder #(.width(32)) adder_1 (.a(PC), .b(Imm), .out(adder_1_out));  // open: cin, cout
  Multiplexer #(.width(32), .enable("false")) multiplexer_1 (
    .in0(PC___4), .in1(adder_1_out), .out(multiplexer_1_out), .sel(PCSrc));
  // Probe on Imm
  contador contador_1 (.Clock(CLK), .Contador(contador_1_contador));
  Clock clock_1 (.out(CLK));
  Multiplexer #(.width(32), .enable("false")) multiplexer_2 (
    .in0(multiplexer_1_out), .in1(ULA), .out(multiplexer_2_out), .sel(Jalr));
  // Probe on contador_1_contador
  Register #(.width(32)) u_PC (.D(multiplexer_2_out), .Q(PC), .clk(CLK));  // open: en, clr
  // Probe on PC
  // Probe on LD1
  // Probe on LD2
  // Probe on ULA
  Adder #(.width(32)) adder_2 (.a(32'h4), .b(PC), .out(PC___4));  // open: cin, cout
  MemInstr meminstr_1 (.PC_address(PC), .Instruction(meminstr_1_instruction));
  decodificador decodificador_1 (
    .\instrução (meminstr_1_instruction), .opcode(decodificador_1_opcode), .rd(decodificador_1_rd),
    .funct3(decodificador_1_funct3), .rs1(decodificador_1_rs1), .rs2(decodificador_1_rs2),
    .funct7(decodificador_1_funct7));
  // Probe on decodificador_1_opcode
  immGen immgen_1 (.\instrução (meminstr_1_instruction), .imm(Imm), .ImmSrc(ImmSrc));
  // Probe on decodificador_1_rs1
  // Probe on decodificador_1_rs2
  ucULA ucula_1 (
    .funct7(decodificador_1_funct7), .funct3(decodificador_1_funct3), .ALUOp(ALUOp), .Bne(Bne),
    .ALUControl(ucula_1_alucontrol));
  ucPrincipal ucprincipal_1 (
    .opcode(decodificador_1_opcode), .RegWrite(RegWrite), .ALUSrc(ALUSrc), .MemToReg(MemToReg),
    .MemRead(MemRead), .MemWrite(MemWrite), .PCSrc(PCSrc), .Branch(Branch), .ALUOp(ALUOp), .Zero(Zero),
    .Bne(Bne), .Jalr(Jalr), .Jump(Jump), .ImmSrc(ImmSrc));
  // Probe on decodificador_1_rd
  Multiplexer #(.width(32), .enable("false")) multiplexer_3 (
    .in0(WD), .in1(PC___4), .out(multiplexer_3_out), .sel(Jump));
  bancoRegistradores bancoregistradores_1 (
    .WD(multiplexer_3_out), .WR(decodificador_1_rd), .LD1(LD1), .LR1(decodificador_1_rs1),
    .LD2(bancoregistradores_1_ld2), .LR2(decodificador_1_rs2), .clk(CLK), .RegWrite(RegWrite));
  Multiplexer #(.width(32), .enable("false")) multiplexer_4 (
    .in0(bancoregistradores_1_ld2), .in1(Imm), .out(LD2), .sel(ALUSrc));
  ula ula_1 (
    .ZERO(Zero), .Result(ULA), .Overflow(ula_1_overflow), .A(LD1), .B(LD2), .ALUControl(ucula_1_alucontrol),
    .NEG(Neg));
  LED led_1 (.in(ula_1_overflow));
  datamem datamem_1 (
    .Escreve_dado(bancoregistradores_1_ld2), .Endereco(ULA), .MemWrite(MemWrite), .clk(CLK),
    .MemRead(MemRead), .Dados_lidos(datamem_1_dados_lidos));  // open: clear
  Multiplexer #(.width(32), .enable("false")) multiplexer_5 (
    .in0(ULA), .in1(datamem_1_dados_lidos), .out(WD), .sel(MemToReg));

  // Notes on the sheet:
  //   Opcode
  //   rs2
  //   rs1
  //   rd
  //   Overflow
endmodule
